// Logisim project ProyectoMIPS.circ as structural Verilog: 3 circuits, main circuit main
module main (
);

  wire clock_1_out;
  wire [23:0] pc_1_out_3;
  wire [31:0] ram_1_data;

  PC pc_1 (.in_2(clock_1_out), .out_3(pc_1_out_3));  // open: in_1
  Clock clock_1 (.out(clock_1_out));
  RAM #(.addrWidth(24), .dataWidth(32)) ram_1 (.addr(pc_1_out_3), .data(ram_1_data));  // open: sel, clk, ld, clr

  // Notes on the sheet:
  //   FETCH
endmodule

module PC (
  input  in_1,
  input  in_2,
  output [23:0] out_3
);

  wire [23:0] adder_1_out;

  Adder #(.width(24)) adder_1 (.a(out_3), .b(24'h1), .out(adder_1_out));  // open: cin, cout
  Register #(.width(24)) register_1 (.D(adder_1_out), .Q(out_3), .clk(in_2), .clr(in_1));  // open: en
endmodule

module Show (
);

  Multiplexer multiplexer_1 ();  // open: in0, in1, out, sel, en
endmodule
